# Fritzing sketch schematic (saved by Fritzing 0.8.7b)

parts:
  Mega_2560 = Arduino Mega ADK (Rev3)
  Ethernet_card = Arduino Board Ethernet  # not connected
  DHT22_R1 = Humidity and Temperature Sensor RHT03
  DHT22_R2 = Humidity and Temperature Sensor RHT03
  DHT22_R3 = Humidity and Temperature Sensor RHT03
  DHT22_R4 = Humidity and Temperature Sensor RHT03
  U1 = LM2596 step down module
  Any_PSU_(12v?) = Battery

nets:
  N1: Mega_2560.D46, DHT22_R1.GND_2
  N2: Mega_2560.D47, DHT22_R2.GND_2
  N3: Mega_2560.D48, DHT22_R3.GND_2
  N4: Mega_2560.D49, DHT22_R4.GND_2
  N5: DHT22_R1.Data-signal, DHT22_R2.Data-signal, DHT22_R4.Data-signal, U1.OUT+
  N6: DHT22_R1.GND_1, DHT22_R2.GND_1, DHT22_R3.GND_1, DHT22_R4.GND_1, U1.IN-, U1.OUT-, Any_PSU_(12v?).-
  N7: U1.IN+, Any_PSU_(12v?).+

custom parts:
  LM2596 step down module: LM2596 DC-DC step down power supply module 3 A.
